# Fritzing sketch Bluetooth Module (saved by Fritzing 0.9.3b)
breadboards: 1

parts:
  Componente1 = Arduino Uno (Rev3)
  Componente2 = Bluetooth HC-05 Macho
  LED1 = LED - 5mm [color="Red (633nm)" package="5 mm [THT]"]
  R1 = Resistor [tolerance=±5% resistance=220 package=THT]

nets:
  N1: Componente1.D13/SCK, LED1.anode
  N2: Componente1.D0/RX, Componente2.TXD
  N3: Componente1.D1/TX, Componente2.RXD
  5V: Componente1.5V, Componente2.VCC
  GND: Componente1.GND, Componente2.GND, R1.Pin_1
  N4: LED1.cathode, R1.Pin_0
